# Fritzing sketch circuit (saved by Fritzing 0.9.6b)
breadboards: 1

parts:
  U1 = ESP32S-HiLetgo [part_number=ESP32S-HiLetgo]
  Componente1 = RFID-RC522-v2
  M1 = fc-51 [package=THT]
  LED1 = LED - 5mm [color="Red (633nm)" current=0.030 package="5 mm [THT]"]
  LED2 = LED - 5mm [color="Green (555nm)" current=0.030 package="5 mm [THT]"]
  J1 = Piezo Speaker
  R1 = Resistor [tolerance=±5% power=0.25 resistance=470 package=THT]
  R2 = Resistor [tolerance=±5% power=0.25 resistance=470 package=THT]
  LCD2004-I2C1 = LCD2004-I2C
  J2 = Basic Servo

nets:
  N1: U1.3.3, Componente1.3.3V
  N2: U1.GPIO36, J1.pin2
  GND: U1.GND, Componente1.GND, M1.pin2, LED1.cathode, LED2.cathode, J1.pin1, LCD2004-I2C1.GND, J2.gnd
  N3: U1.GPIO13, J2.pulse
  VCC: U1.VIN, M1.pin3, LCD2004-I2C1.VCC, J2.vcc
  N4: U1.GPIO7, R2.Pin_0
  N5: U1.GPIO8, R1.Pin_0
  N6: U1.GPIO15, Componente1.RST
  N7: U1.GPIO4, Componente1.SDA
  N8: U1.GPIO17, M1.pin1
  N9: U1.GPIO18, Componente1.SCK
  N10: U1.GPIO19, Componente1.MISO
  N11: U1.GPIO21, LCD2004-I2C1.SDA
  N12: U1.GPIO22, LCD2004-I2C1.SCL
  N13: U1.GPIO23, Componente1.MOSI
  N14: LED1.anode, R1.Pin_1
  N15: LED2.anode, R2.Pin_1

custom parts:
  ESP32S-HiLetgo: HiLetgo ESP-WROOM-32 ESP32 ESP-32S Development Board 2.4GHz Dual-Mode WiFi + Bluetooth Dual Cores Microcontroller The ESP32 integrated with Antenna switches, RF Balun, power amplifiers, low-noise amplifiers, filters, and management modules, and the entire solution occupies the least area of PCB. 2.4 GHz Wi-Fi plus Bluetooth dual-mode chip, with TSMC Ultra-low power consumption 40nm technology,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
  RFID-RC522-v2: A simple China made RFID-RC522 Reader; do check the pin labels, as this is a MFRC522 based clone.
  LCD2004-I2C: A standard character display with 4x20 characters. Comes in many colors with LCM2004 IIC attached.

// code stored in the sketch: main.ino
#include <Wire.h>
#include <LiquidCrystal_I2C.h>
#include <MFRC522.h>
#include <Servo.h>

#define LED_VERDE 7
#define LED_VERMELHO 8
#define BUZZER 36
#define SENSOR_FC51 17
#define SERVO_PIN 13

#define RST_PIN 15
#define SS_PIN 4

LiquidCrystal_I2C lcd(0x27, 20, 4);
MFRC522 rfid(SS_PIN, RST_PIN);
Servo servoMotor;

const char* validIDs[] = {"1234567890", "0987654321", "1122334455"};
const int maxInvalidAttempts = 3;

int vagasDisponiveis = 1;
int invalidAttempts = 0;

void setup() 
{
  Serial.begin(115200);

  pinMode(LED_VERDE, OUTPUT);
  pinMode(LED_VERMELHO, OUTPUT);
  pinMode(BUZZER, OUTPUT);
  pinMode(SENSOR_FC51, INPUT);
  servoMotor.attach(SERVO_PIN);

  lcd.begin();
  lcd.backlight();
  lcd.setCursor(0, 0);
  lcd.print("SISTEMA DE ESTACIONAMENTO");

  SPI.begin();
  rfid.PCD_Init();

  servoMotor.write(0);

  atualizaStatusVagas();
}

void loop() 
{
  monitorarVagas();

  if (vagasDisponiveis > 0) 
	{
    if (rfid.PICC_IsNewCardPresent() && rfid.PICC_ReadCardSerial()) 
		{
      String idCartao = leCartaoRFID();
      validaCartao(idCartao);
      rfid.PICC_HaltA();
    }
  }

  delay(500);
}

void atualizaStatusVagas() 
{
  lcd.setCursor(0, 1);

  if (vagasDisponiveis > 0) 
	{
    lcd.print("VAGAS DISPONIVEIS: ");
    lcd.print(vagasDisponiveis);
  } 
	else 
	{
    lcd.print("VAGAS INDISPONIVEIS");
  }
}

String leCartaoRFID() 
{
  String conteudo = "";

  for (byte i = 0; i < rfid.uid.size; i++) 
	{
    conteudo += String(rfid.uid.uidByte[i], HEX);
  }

  conteudo.toUpperCase();
  return conteudo;
}

void validaCartao(String id) 
{
  bool valido = false;

  for (int i = 0; i < sizeof(validIDs) / sizeof(validIDs[0]); i++) 
	{
    if (id == validIDs[i]) 
		{
      valido = true;
      break;
    }
  }

  if (valido) 
	{
    acessoLiberado(id);
  } 
	else 
	{
    acessoNegado();
  }
}

void acessoLiberado(String id) 
{
  lcd.clear();
  lcd.setCursor(0, 0);
  lcd.print("ACESSO LIBERADO");
  lcd.setCursor(0, 1);
  lcd.print("ID DO CARTAO: ");
  lcd.print(id);

  digitalWrite(LED_VERDE, HIGH);
  servoMotor.write(90); 

  delay(2000); 

  servoMotor.write(0); 

  digitalWrite(LED_VERDE, LOW);

  vagasDisponiveis--;
  atualizaStatusVagas();
}

void acessoNegado() 
{
  lcd.clear();
  lcd.setCursor(0, 0);
  lcd.print("ACESSO NEGADO");

  digitalWrite(LED_VERMELHO, HIGH);
  delay(500);
  digitalWrite(LED_VERMELHO, LOW);
  delay(500);
  digitalWrite(LED_VERMELHO, HIGH);
  delay(500);
  digitalWrite(LED_VERMELHO, LOW);

  invalidAttempts++;

  if (invalidAttempts >= maxInvalidAttempts) 
	{
    tone(BUZZER, 1000, 2000); 
    lcd.setCursor(0, 1);
    lcd.print("TENTATIVAS EXCEDIDAS");
  }
}

void monitorarVagas() 
{
  int estadoSensor = digitalRead(SENSOR_FC51);

  if (estadoSensor == LOW && vagasDisponiveis < 1) 
	{
    vagasDisponiveis++;
    atualizaStatusVagas();
  }
}
