# Fritzing sketch projeto-circuito (saved by Fritzing 0.9.6b)
breadboards: 1

parts:
  U1 = ESP32S-HiLetgo [part_number=ESP32S-HiLetgo]
  Componente1 = RFID-RC522-v2
  M1 = fc-51 [package=THT]
  LED1 = LED - 5mm [color="Red (633nm)" current=0.030 package="5 mm [THT]"]
  LED2 = LED - 5mm [color="Green (555nm)" current=0.030 package="5 mm [THT]"]
  J1 = Piezo Speaker
  R1 = Resistor [tolerance=±5% power=0.25 resistance=470 package=THT]
  R2 = Resistor [tolerance=±5% power=0.25 resistance=470 package=THT]
  LCD2004-I2C1 = LCD2004-I2C
  J2 = Basic Servo

nets:
  N1: U1.3.3, Componente1.3.3V
  N2: U1.GPIO36, J1.pin2
  GND: U1.GND, Componente1.GND, M1.pin2, LED1.cathode, LED2.cathode, J1.pin1, LCD2004-I2C1.GND, J2.gnd
  N3: U1.GPIO13, J2.pulse
  VCC: U1.VIN, M1.pin3, LCD2004-I2C1.VCC, J2.vcc
  N4: U1.GPIO7, R2.Pin_0
  N5: U1.GPIO8, R1.Pin_0
  N6: U1.GPIO15, Componente1.RST
  N7: U1.GPIO4, Componente1.SDA
  N8: U1.GPIO17, M1.pin1
  N9: U1.GPIO18, Componente1.SCK
  N10: U1.GPIO19, Componente1.MISO
  N11: U1.GPIO21, LCD2004-I2C1.SDA
  N12: U1.GPIO22, LCD2004-I2C1.SCL
  N13: U1.GPIO23, Componente1.MOSI
  N14: LED1.anode, R1.Pin_1
  N15: LED2.anode, R2.Pin_1

custom parts:
  ESP32S-HiLetgo: HiLetgo ESP-WROOM-32 ESP32 ESP-32S Development Board 2.4GHz Dual-Mode WiFi + Bluetooth Dual Cores Microcontroller The ESP32 integrated with Antenna switches, RF Balun, power amplifiers, low-noise amplifiers, filters, and management modules, and the entire solution occupies the least area of PCB. 2.4 GHz Wi-Fi plus Bluetooth dual-mode chip, with TSMC Ultra-low power consumption 40nm technology,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
  RFID-RC522-v2: A simple China made RFID-RC522 Reader; do check the pin labels, as this is a MFRC522 based clone.
  LCD2004-I2C: A standard character display with 4x20 characters. Comes in many colors with LCM2004 IIC attached.
